// Logisim project archi_logic.circ as structural Verilog: 18 circuits, main circuit decoder2bit
module decoder2bit (
  input  s1,
  input  s0,
  output y0,
  output y1,
  output y2,
  output y3
);

  and and_1 (y0, ~s1, ~s0);  // AND_Gate
  and and_2 (y1, ~s1, s0);  // AND_Gate
  and and_3 (y2, s1, ~s0);  // AND_Gate
  and and_4 (y3, s1, s0);
endmodule

module andBitwise4 (
  input  b4,
  input  a3,
  input  b2,
  input  a2,
  input  b1,
  input  a1,
  input  b0,
  input  a0,
  output y3,
  output y2,
  output y1,
  output y0
);

  and and_1 (y3, b4, a3);
  and and_2 (y2, b2, a2);
  and and_3 (y1, b1, a1);
  and and_4 (y0, b0, a0);
endmodule

module multiplexer4bit (
  input  [3:0] x,
  input  s1,
  input  s0,
  output y
);

  wire andbitwise4_1_y0, andbitwise4_1_y1, andbitwise4_1_y2, andbitwise4_1_y3;
  wire [3:0] decoder2bit_1_y0;

  decoder2bit decoder2bit_1 (
    .s1(s1), .s0(s0), .y0(decoder2bit_1_y0[0]), .y1(decoder2bit_1_y0[1]), .y2(decoder2bit_1_y0[2]),
    .y3(decoder2bit_1_y0[3]));
  andBitwise4 andbitwise4_1 (
    .b4(x[3]), .a3(decoder2bit_1_y0[3]), .b2(x[2]), .a2(decoder2bit_1_y0[2]), .b1(x[1]),
    .a1(decoder2bit_1_y0[1]), .b0(x[0]), .a0(decoder2bit_1_y0[0]), .y3(andbitwise4_1_y3),
    .y2(andbitwise4_1_y2), .y1(andbitwise4_1_y1), .y0(andbitwise4_1_y0));
  or or_1 (y, andbitwise4_1_y3, andbitwise4_1_y2, andbitwise4_1_y1, andbitwise4_1_y0);
endmodule

module halfadder (
  input  a,
  input  b,
  output r,
  output y
);

  and and_1 (r, a, b);
  xor xor_1 (y, a, b);
endmodule

module fulladder (
  input  rin,
  input  a,
  input  b,
  output rout,
  output y
);

  wire halfadder_1_r, halfadder_1_y, halfadder_2_r;

  halfadder halfadder_1 (.a(a), .b(b), .r(halfadder_1_r), .y(halfadder_1_y));
  halfadder halfadder_2 (.a(rin), .b(halfadder_1_y), .r(halfadder_2_r), .y(y));
  or or_1 (rout, halfadder_1_r, halfadder_2_r);
endmodule

module adder4bit (
  input  [3:0] b,
  input  [3:0] a,
  input  rin,
  output rout,
  output [3:0] y
);

  wire fulladder_2_rout, fulladder_3_rout, fulladder_4_rout;

  fulladder fulladder_1 (.rin(b[3]), .a(a[3]), .b(fulladder_2_rout), .rout(rout), .y(y[3]));
  fulladder fulladder_2 (.rin(b[2]), .a(a[2]), .b(fulladder_3_rout), .rout(fulladder_2_rout), .y(y[2]));
  fulladder fulladder_3 (.rin(b[1]), .a(a[1]), .b(fulladder_4_rout), .rout(fulladder_3_rout), .y(y[1]));
  fulladder fulladder_4 (.rin(b[0]), .a(a[0]), .b(rin), .rout(fulladder_4_rout), .y(y[0]));
endmodule

module complemento1 (
  input  [3:0] a,
  output [3:0] y
);

  not not_1 (y[0], a[0]);
  not not_2 (y[1], a[1]);
  not not_3 (y[2], a[2]);
  not not_4 (y[3], a[3]);
endmodule

module complemento2 (
  input  [3:0] a,
  output rout,
  output [3:0] y
);

  wire [3:0] complemento1_1_y;

  complemento1 complemento1_1 (.a(a), .y(complemento1_1_y));
  incr1for4bit incr1for4bit_1 (.a(complemento1_1_y), .i(1'b1), .rout(rout), .y(y));
endmodule

module incr1for4bit (
  input  [3:0] a,
  input  i,
  output rout,
  output [3:0] y
);

  wire halfadder_2_r, halfadder_3_r, halfadder_4_r;

  halfadder halfadder_1 (.a(a[3]), .b(halfadder_2_r), .r(rout), .y(y[3]));
  halfadder halfadder_2 (.a(a[2]), .b(halfadder_3_r), .r(halfadder_2_r), .y(y[2]));
  halfadder halfadder_3 (.a(a[1]), .b(halfadder_4_r), .r(halfadder_3_r), .y(y[1]));
  halfadder halfadder_4 (.a(a[0]), .b(i), .r(halfadder_4_r), .y(y[0]));
endmodule

module sommaDifferenza (
  input  [3:0] a,
  input  [3:0] b,
  input  op0,
  output rout,
  output [3:0] y,
  output error
);

  wire [3:0] incr1for4bit_1_y, notpilotabile_1_y;

  notPilotabile notpilotabile_1 (.a(b), .enable(op0), .y(notpilotabile_1_y));
  incr1for4bit incr1for4bit_1 (.a(notpilotabile_1_y), .i(op0), .y(incr1for4bit_1_y));  // open: rout
  adder4bit adder4bit_1 (.b(a), .a(incr1for4bit_1_y), .rin(1'b0), .rout(rout), .y(y));
  overflowDetecter overflowdetecter_1 (.b(b[3]), .a(a[3]), .y(y[3]));  // open: overflow
endmodule

module notPilotabile (
  input  [3:0] a,
  input  enable,
  output [3:0] y
);

  xor xor_1 (y[3], a[3], enable);
  xor xor_2 (y[2], a[2], enable);
  xor xor_3 (y[1], a[1], enable);
  xor xor_4 (y[0], a[0], enable);
endmodule

module overflowDetecter (
  input  b,
  input  a,
  input  y,
  output overflow
);

  wire xor_1_out, xor_2_out;

  xor xor_1 (xor_1_out, b, y);
  xor xor_2 (xor_2_out, a, y);
  and and_1 (overflow, xor_1_out, xor_2_out);
endmodule

module mult4bit (
  input  [3:0] a,
  input  [3:0] b,
  output r,
  output [3:0] high,
  output [3:0] low
);

  wire fulladder_1_rout, fulladder_1_y, fulladder_2_rout, fulladder_2_y, fulladder_3_rout, fulladder_3_y,
       fulladder_4_rout, fulladder_4_y, fulladder_5_rout, fulladder_6_rout, fulladder_7_rout, halfadder_1_r,
       halfadder_1_y, halfadder_2_r, halfadder_3_r, halfadder_3_y, halfadder_4_r, halfadder_4_y,
       halfadder_6_r, halfadder_7_r;
  wire [3:0] and4bitfor1bit_1_y, and4bitfor1bit_2_y, and4bitfor1bit_3_y;
  wire [3:1] and4bitfor1bit_4_y;

  and4bitFor1bit and4bitfor1bit_1 (.f(b[3]), .a(a), .y(and4bitfor1bit_1_y));
  and4bitFor1bit and4bitfor1bit_2 (.f(b[2]), .a(a), .y(and4bitfor1bit_2_y));
  and4bitFor1bit and4bitfor1bit_3 (.f(b[1]), .a(a), .y(and4bitfor1bit_3_y));
  and4bitFor1bit and4bitfor1bit_4 (.f(b[0]), .a(a), .y({and4bitfor1bit_4_y, low[0]}));
  halfadder halfadder_1 (.a(and4bitfor1bit_1_y[3]), .b(fulladder_1_rout), .r(halfadder_1_r), .y(halfadder_1_y));
  halfadder halfadder_2 (.a(and4bitfor1bit_3_y[0]), .b(and4bitfor1bit_4_y[1]), .r(halfadder_2_r), .y(low[1]));
  fulladder fulladder_1 (
    .rin(and4bitfor1bit_1_y[2]), .a(and4bitfor1bit_2_y[3]), .b(fulladder_2_rout), .rout(fulladder_1_rout),
    .y(fulladder_1_y));
  fulladder fulladder_2 (
    .rin(and4bitfor1bit_1_y[1]), .a(and4bitfor1bit_2_y[2]), .b(halfadder_3_r), .rout(fulladder_2_rout),
    .y(fulladder_2_y));
  fulladder fulladder_3 (
    .rin(and4bitfor1bit_3_y[1]), .a(and4bitfor1bit_4_y[2]), .b(halfadder_2_r), .rout(fulladder_3_rout),
    .y(fulladder_3_y));
  halfadder halfadder_3 (.a(and4bitfor1bit_1_y[0]), .b(and4bitfor1bit_2_y[1]), .r(halfadder_3_r), .y(halfadder_3_y));
  fulladder fulladder_4 (
    .rin(and4bitfor1bit_3_y[2]), .a(and4bitfor1bit_4_y[3]), .b(fulladder_3_rout), .rout(fulladder_4_rout),
    .y(fulladder_4_y));
  halfadder halfadder_4 (.a(and4bitfor1bit_3_y[3]), .b(fulladder_4_rout), .r(halfadder_4_r), .y(halfadder_4_y));
  halfadder halfadder_5 (.a(halfadder_1_r), .b(halfadder_6_r), .r(r), .y(high[3]));
  halfadder halfadder_6 (.a(halfadder_1_y), .b(fulladder_5_rout), .r(halfadder_6_r), .y(high[2]));
  fulladder fulladder_5 (
    .rin(fulladder_1_y), .a(halfadder_4_r), .b(fulladder_6_rout), .rout(fulladder_5_rout), .y(high[1]));
  fulladder fulladder_6 (
    .rin(fulladder_2_y), .a(halfadder_4_y), .b(fulladder_7_rout), .rout(fulladder_6_rout), .y(high[0]));
  fulladder fulladder_7 (
    .rin(halfadder_3_y), .a(fulladder_4_y), .b(halfadder_7_r), .rout(fulladder_7_rout), .y(low[3]));
  halfadder halfadder_7 (.a(and4bitfor1bit_2_y[0]), .b(fulladder_3_y), .r(halfadder_7_r), .y(low[2]));
endmodule

module and4bitFor1bit (
  input  f,
  input  [3:0] a,
  output [3:0] y
);

  and and_1 (y[0], f, a[0]);
  and and_2 (y[1], f, a[1]);
  and and_3 (y[2], f, a[2]);
  and and_4 (y[3], f, a[3]);
endmodule

module latchSR (
  input  S,
  input  R,
  output Q_,
  output Q
);

  nor nor_1 (Q_, S, Q);
  nor nor_2 (Q, Q_, R);
endmodule

module latchSincronoSR (
  input  s,
  input  r,
  input  clk,
  output Q_,
  output Q
);

  wire and_1_out, and_2_out;

  and and_1 (and_1_out, s, clk);
  and and_2 (and_2_out, r, clk);
  latchSR latchsr_1 (.S(and_1_out), .R(and_2_out), .Q_(Q_), .Q(Q));
endmodule

module latchSincronoD (
  input  D,
  input  clk,
  output Q_,
  output Q
);

  wire not_1_out;

  not not_1 (not_1_out, D);
  latchSincronoSR latchsincronosr_1 (.s(D), .r(not_1_out), .clk(clk), .Q_(Q_), .Q(Q));
endmodule

module register4bit (
  input  [3:0] d,
  input  reset,
  input  write,
  input  clk,
  output [3:0] Q
);

  wire and_1_out, not_1_out, or_1_out;
  wire [3:0] and4bitfor1bit_1_y;

  not not_1 (not_1_out, reset);
  and4bitFor1bit and4bitfor1bit_1 (.f(not_1_out), .a(d), .y(and4bitfor1bit_1_y));
  and and_1 (and_1_out, write, clk);
  or or_1 (or_1_out, reset, and_1_out);
  latchSincronoD latchsincronod_1 (.D(and4bitfor1bit_1_y[3]), .clk(or_1_out), .Q(Q[3]));  // open: Q_
  latchSincronoD latchsincronod_2 (.D(and4bitfor1bit_1_y[2]), .clk(or_1_out), .Q(Q[2]));  // open: Q_
  latchSincronoD latchsincronod_3 (.D(and4bitfor1bit_1_y[1]), .clk(or_1_out), .Q(Q[1]));  // open: Q_
  latchSincronoD latchsincronod_4 (.D(and4bitfor1bit_1_y[0]), .clk(or_1_out), .Q(Q[0]));  // open: Q_
endmodule
